# Fritzing sketch LedTestScheme (saved by Fritzing 0.9.3b)
breadboards: 1

parts:
  MOTOR1 = 28BYJ-48 Stepper Motor
  Part1 = Arduino Mega 2560 (Rev3)
  Part2 = KY-003 Hall Magnetic Sensor Module [package="Breakout board"]
  Part3 = EasyDriver_v44
  Part4 = EasyDriver_v44
  R3 = Resistor [tolerance=±5% resistance=220 package=THT]  # not connected
  R4 = Resistor [tolerance=±5% resistance=220 package=THT]  # not connected
  LED1 = LED - 5mm [color="Red (633nm)" package="5 mm [THT]"]
  M1 = Stepper Motor - Bipolar
  Power_plug1 = Power plug
  R5 = Resistor [tolerance=±5% resistance=220 package=THT]
  P1 = S1133 Si Photodiode [package="8mm Ceramic [THT]"]  # not connected
  P2 = S1133 Si Photodiode [package="8mm Ceramic [THT]"]  # not connected

nets:
  N1: MOTOR1.ORANGE, Part4.OUT1B
  N2: MOTOR1.YELLOW, Part4.OUT1A
  N3: MOTOR1.PINK, Part4.OUT2B
  N4: MOTOR1.BLUE, Part4.OUT2A
  GND: Part1.GND, Part2.-, Part3.GND, Part4.GND, LED1.cathode, Power_plug1.GND
  N5: Part1.D13_PWM, Part3.STEP
  N6: Part1.D12_PWM, Part3.DIR
  N7: Part1.D11_PWM, Part4.STEP
  N8: Part1.D10_PWM, Part4.DIR
  5V: Part1.5V, Part2.Vin
  N9: Part1.D7_PWM, Part2.S
  N10: Part1.D31, R5.Pin_0
  N11: Part3.V+, Part4.V+, Power_plug1.VCC
  N12: Part3.OUT2A, M1.A
  N13: Part3.OUT2B, M1.C
  N14: Part3.OUT1A, M1.B
  N15: Part3.OUT1B, M1.D
  N16: LED1.anode, R5.Pin_1

notes:
  12V

custom parts:
  KY-003 Hall Magnetic Sensor Module: KEYES KY-003 Arduino Hall Magnetic Sensor Module is a switch that will turn on/off in the presence of a magnetic field.
